# Fritzing sketch ardularm (saved by Fritzing 0.9.3b)
breadboards: 1

parts:
  Часть1 = Arduino Uno (Rev3)
  R1_(PUR) = Resistor [tolerance=±5% resistance=10k package=THT]
  ALM = LED - 5mm [color="Red (633nm)" package="5 mm [THT]"]
  NORM = LED - 5mm [color="Green (555nm)" package="5 mm [THT]"]
  SPV = LED - 5mm [color="Blue (430nm)" package="5 mm [THT]"]
  STROBE = RELAY [package=relay-g5q]
  HORN = RELAY [package=relay-g5q]
  SIL = LED - 5mm [color="Yellow (595nm)" package="5 mm [THT]"]
  R3 = Resistor [tolerance=±5% resistance=1k package=THT]
  R4 = Resistor [tolerance=±5% resistance=1k package=THT]
  R5 = Resistor [tolerance=±5% resistance=1k package=THT]
  R6 = Resistor [tolerance=±5% resistance=1k package=THT]
  PULL_ST = Round Pushbutton
  R7_(PUR) = Resistor [tolerance=±5% resistance=10k package=THT]
  R8_(EOL) = Resistor [tolerance=±5% resistance=10k package=THT]
  KEY_SW = Round Pushbutton
  J1 = Piezo Speaker
  SIL_2 = Square Pushbutton
  R9 = Resistor [tolerance=±5% resistance=10k package=THT]
  J3 = Screw terminal - 2 pins [package=THT]
  ACK = Square Pushbutton
  J2 = Screw terminal - 2 pins [package=THT]

nets:
  N1: Часть1.A0, R1_(PUR).Pin_0, SIL_2.leg1, ACK.leg1
  N2: Часть1.A1, PULL_ST.leg0, R7_(PUR).Pin_0, R8_(EOL).Pin_0
  N3: Часть1.D8, STROBE.COIL1
  N4: Часть1.GND, R1_(PUR).Pin_1, ALM.cathode, NORM.cathode, SPV.cathode, STROBE.COIL2, HORN.COIL2, SIL.cathode, R7_(PUR).Pin_1, KEY_SW.leg0, J1.pin1
  N5: Часть1.D1/TX, R6.Pin_1
  N6: Часть1.D2, R5.Pin_1
  N7: Часть1.D3_PWM, R4.Pin_1
  N8: Часть1.D4, R3.Pin_1
  N9: Часть1.D5_PWM, J1.pin2
  N10: Часть1.D7, HORN.COIL1
  N11: Часть1.RESET, KEY_SW.leg1
  N12: Часть1.5V, PULL_ST.leg1, R8_(EOL).Pin_1, SIL_2.leg0, R9.Pin_0
  N13: ALM.anode, R5.Pin_0
  N14: NORM.anode, R4.Pin_0
  N15: SPV.anode, R6.Pin_0
  N16: STROBE.MAIN, J3.pin1
  N17: STROBE.NO, J3.pin2
  N18: HORN.MAIN, J2.pin1
  N19: HORN.NO, J2.pin2
  N20: SIL.anode, R3.Pin_0
  N21: R9.Pin_1, ACK.leg0

notes:
  Ardularm, PUR - pull up resistor, EOL - end of line, v 3.0
